// Logisim project ArrayMultiplier2X2.circ as structural Verilog: 2 circuits, main circuit main
module main (
  input  a0,
  input  a1,
  input  b0,
  input  b1,
  output out_5,
  output out_6,
  output out_7,
  output out_8
);

  multiplier2X2 multiplier2x2_1 (
    .a0(a0), .a1(a1), .b0(b0), .b1(b1), .p_0(out_5), .p_1(out_6), .p_2(out_7), .p_3(out_8));
endmodule

module multiplier2X2 (
  input  a0,
  input  a1,
  input  b0,
  input  b1,
  output p_0,
  output p_1,
  output p_2,
  output p_3
);

  wire and_2_out, and_3_out, and_4_out, and_5_out;

  and and_1 (p_0, a0, b0);
  and and_2 (and_2_out, a1, b0);
  and and_3 (and_3_out, a0, b1);
  and and_4 (and_4_out, a1, b1);
  xor xor_1 (p_1, and_2_out, and_3_out);
  and and_5 (and_5_out, and_2_out, and_3_out);
  and and_6 (p_3, and_5_out, and_4_out);
  xor xor_2 (p_2, and_5_out, and_4_out);

  // Notes on the sheet:
  //   pp0
  //   pp1
  //   pp2
  //   pp3
  //   s1
  //   c1
  //   c2
  //   s2
endmodule
