// Logisim project ALUsandeep.circ as structural Verilog: 3 circuits, main circuit main
module main (
  input  Update_Flags,
  input  [7:0] in_2,
  input  [7:0] in_3,
  input  Update_o_p,
  input  in_5,
  output N,
  output Z,
  output C,
  output V,
  output [7:0] result
);

  wire [3:0] add8bit_1_n_z_c_v, multiplexer_1_out, sub8bit_1_n_z_c_v;
  wire [7:0] add8bit_1_out_5, multiplexer_2_out, sub8bit_1_out_5;

  add8bit add8bit_1 (.in_1(in_2), .in_2(in_3), .in_3(in_5), .N_Z_C_V(add8bit_1_n_z_c_v), .out_5(add8bit_1_out_5));
  sub8bit sub8bit_1 (.in_1(in_2), .in_2(in_3), .in_3(in_5), .N_Z_C_V(sub8bit_1_n_z_c_v), .out_5(sub8bit_1_out_5));
  Multiplexer #(.width(4)) multiplexer_1 (
    .in0(add8bit_1_n_z_c_v), .in1(sub8bit_1_n_z_c_v), .out(multiplexer_1_out), .sel(in_5));
  Multiplexer #(.width(8)) multiplexer_2 (
    .in0(add8bit_1_out_5), .in1(sub8bit_1_out_5), .out(multiplexer_2_out), .sel(in_5));
  Register #(.width(4)) register_1 (.D(multiplexer_1_out), .clk(Update_Flags), .Q({N, Z, C, V}));  // open: en, clr
  Register register_2 (.D(multiplexer_2_out), .clk(Update_o_p), .Q(result));  // open: en, clr

  // Notes on the sheet:
  //   A [7:0]
  //   B[7:0]
  //   flags
  //   result
  //   flags
  //   result
  //   flag mux
  //   Operation
  //   0 - add
  //   1 - sub
  //   result mux
  //   Status Reg
  //   flags
endmodule

module add8bit (
  input  [7:0] in_1,
  input  [7:0] in_2,
  input  in_3,
  output [3:0] N_Z_C_V,
  output [7:0] out_5
);

  wire adder_1_cout, adder_2_cout, adder_3_cout, adder_4_cout, adder_5_cout, adder_6_cout, adder_7_cout,
       not_1_out;
  wire [7:0] register_1_q, register_2_q;

  not not_1 (not_1_out, in_3);
  Register register_1 (.D(in_1), .clk(not_1_out), .Q(register_1_q));  // open: en, clr
  Register register_2 (.D(in_2), .clk(not_1_out), .Q(register_2_q));  // open: en, clr
  Adder #(.width(1)) adder_1 (
    .a(register_1_q[0]), .b(register_2_q[0]), .out(out_5[0]), .cin(1'b0), .cout(adder_1_cout));
  Adder #(.width(1)) adder_2 (
    .a(register_1_q[1]), .b(register_2_q[1]), .out(out_5[1]), .cin(adder_1_cout), .cout(adder_2_cout));
  Adder #(.width(1)) adder_3 (
    .a(register_1_q[2]), .b(register_2_q[2]), .out(out_5[2]), .cin(adder_2_cout), .cout(adder_3_cout));
  Adder #(.width(1)) adder_4 (
    .a(register_1_q[3]), .b(register_2_q[3]), .out(out_5[3]), .cin(adder_3_cout), .cout(adder_4_cout));
  Adder #(.width(1)) adder_5 (
    .a(register_1_q[4]), .b(register_2_q[4]), .out(out_5[4]), .cin(adder_4_cout), .cout(adder_5_cout));
  Adder #(.width(1)) adder_6 (
    .a(register_1_q[5]), .b(register_2_q[5]), .out(out_5[5]), .cin(adder_5_cout), .cout(adder_6_cout));
  Adder #(.width(1)) adder_7 (
    .a(register_1_q[6]), .b(register_2_q[6]), .out(out_5[6]), .cin(adder_6_cout), .cout(adder_7_cout));
  Adder #(.width(1)) adder_8 (
    .a(register_1_q[7]), .b(register_2_q[7]), .out(N_Z_C_V[3]), .cin(adder_7_cout), .cout(N_Z_C_V[1]));
  xor xor_1 (N_Z_C_V[0], adder_7_cout, N_Z_C_V[1]);
  Comparator comparator_1 (.a({N_Z_C_V[3], out_5[6:0]}), .b({8{1'b0}}), .eq(N_Z_C_V[2]));  // open: gt, lt

  assign out_5[7] = N_Z_C_V[3];
endmodule

module sub8bit (
  input  [7:0] in_1,
  input  [7:0] in_2,
  input  in_3,
  output [3:0] N_Z_C_V,
  output [7:0] out_5
);

  wire adder_2_cout, adder_3_cout, adder_4_cout, adder_5_cout, adder_6_cout, adder_7_cout, adder_8_cout;
  wire [7:0] adder_1_out, not_1_out, register_1_q, register_2_q;

  Register register_1 (.D(in_2), .clk(in_3), .Q(register_1_q));  // open: en, clr
  Register register_2 (.D(in_1), .clk(in_3), .Q(register_2_q));  // open: en, clr
  assign not_1_out = ~register_1_q;  // NOT_Gate not_1, 8 bits wide
  Adder adder_1 (.a(not_1_out), .b(8'h1), .out(adder_1_out));  // open: cin, cout
  Adder #(.width(1)) adder_2 (.a(register_2_q[0]), .b(adder_1_out[0]), .out(out_5[0]), .cin(1'b0), .cout(adder_2_cout));
  Adder #(.width(1)) adder_3 (
    .a(register_2_q[1]), .b(adder_1_out[1]), .out(out_5[1]), .cin(adder_2_cout), .cout(adder_3_cout));
  Adder #(.width(1)) adder_4 (
    .a(register_2_q[2]), .b(adder_1_out[2]), .out(out_5[2]), .cin(adder_3_cout), .cout(adder_4_cout));
  Adder #(.width(1)) adder_5 (
    .a(register_2_q[3]), .b(adder_1_out[3]), .out(out_5[3]), .cin(adder_4_cout), .cout(adder_5_cout));
  Adder #(.width(1)) adder_6 (
    .a(register_2_q[4]), .b(adder_1_out[4]), .out(out_5[4]), .cin(adder_5_cout), .cout(adder_6_cout));
  Adder #(.width(1)) adder_7 (
    .a(register_2_q[5]), .b(adder_1_out[5]), .out(out_5[5]), .cin(adder_6_cout), .cout(adder_7_cout));
  Adder #(.width(1)) adder_8 (
    .a(register_2_q[6]), .b(adder_1_out[6]), .out(out_5[6]), .cin(adder_7_cout), .cout(adder_8_cout));
  Adder #(.width(1)) adder_9 (
    .a(register_2_q[7]), .b(adder_1_out[7]), .out(N_Z_C_V[3]), .cin(adder_8_cout), .cout(N_Z_C_V[1]));
  xor xor_1 (N_Z_C_V[0], adder_8_cout, N_Z_C_V[1]);
  Comparator comparator_1 (.a({N_Z_C_V[3], out_5[6:0]}), .b({8{1'b0}}), .eq(N_Z_C_V[2]));  // open: gt, lt

  assign out_5[7] = N_Z_C_V[3];
endmodule
