// Logisim project controlUnit.circ as structural Verilog: 1 circuit, main circuit main
module main (
  input  [7:0] in_1,
  input  in_2,
  input  in_3,
  input  [8:0] Opcode,
  input  in_5
);

  wire decoder_1_out0, decoder_1_out1, decoder_1_out2, decoder_1_out3;
  wire [7:0] adder_1_out, multiplexer_1_out, multiplexer_2_out, multiplexer_3_out, register_1_q,
       register_2_q, register_3_q, register_4_q;
  wire [8:0] ram_1_dout, register_5_q;

  Register register_1 (.D(multiplexer_3_out), .en(decoder_1_out0), .clk(in_5), .Q(register_1_q));  // open: clr
  Register register_2 (.D(multiplexer_3_out), .en(decoder_1_out1), .clk(in_5), .Q(register_2_q));  // open: clr
  Register register_3 (.D(multiplexer_3_out), .en(decoder_1_out2), .clk(in_5), .Q(register_3_q));  // open: clr
  Register register_4 (.D(multiplexer_3_out), .en(decoder_1_out3), .clk(in_5), .Q(register_4_q));  // open: clr
  Multiplexer #(.select(2), .width(8)) multiplexer_1 (
    .in0(register_1_q), .in1(register_2_q), .in2(register_3_q), .in3(register_4_q), .out(multiplexer_1_out),
    .sel(ram_1_dout[3:2]));
  Multiplexer #(.select(2), .width(8)) multiplexer_2 (
    .in0(register_1_q), .in1(register_2_q), .in2(register_3_q), .in3(register_4_q), .out(multiplexer_2_out),
    .sel(ram_1_dout[1:0]));
  Adder adder_1 (.a(multiplexer_1_out), .b(multiplexer_2_out), .out(adder_1_out));  // open: cin, cout
  Multiplexer #(.select(3), .width(8)) multiplexer_3 (
    .in0(adder_1_out), .out(multiplexer_3_out), .sel(ram_1_dout[8:6]));  // open: in1, in2, in3, in4, in5, in6, in7
  Register #(.width(9)) register_5 (.D(Opcode), .clk(in_5), .Q(register_5_q));  // open: en, clr
  RAM #(.dataWidth(9)) ram_1 (.addr(in_1), .we(in_2), .oe(in_3), .clk(in_5), .din(register_5_q), .dout(ram_1_dout));
  Decoder #(.select(2)) decoder_1 (
    .out0(decoder_1_out0), .out1(decoder_1_out1), .out2(decoder_1_out2), .out3(decoder_1_out3),
    .sel(ram_1_dout[5:4]));  // open: en

  // Notes on the sheet:
  //   CPU Regissters
  //   R0
  //   R1
  //   R2
  //   R3
  //   src1
  //   src2
  //   Opcode format - opcode(3) destintn(2) src1(2) src2(2)
  //   Result
  //   Opcode
  //   PC
  //   Destntn
  //   Decoder
  //   (Controller)
endmodule
