// Logisim project RAMReadWrite.circ as structural Verilog: 1 circuit, main circuit main
module main (
  input  in_1,
  input  in_2,
  input  [7:0] initial_address,
  input  in_4,
  input  [7:0] in_5,
  input  in_6,
  input  Clk,
  input  Clk_2,
  input  [7:0] in_9,
  input  in_10,
  input  Clk_3,
  output [7:0] out_12
);

  wire [7:0] adder_1_out, multiplexer_1_out, ram_1_dout, register_1_q, register_2_q, register_3_q,
       register_5_q;

  Adder adder_1 (.a(in_5), .b(register_2_q), .out(adder_1_out));  // open: cin, cout
  Multiplexer #(.width(8)) multiplexer_1 (
    .in0(initial_address), .in1(adder_1_out), .out(multiplexer_1_out), .sel(in_6));
  Register register_1 (.D(register_2_q), .en(in_1), .clk(Clk_2), .Q(register_1_q));  // open: clr
  Register register_2 (.D(multiplexer_1_out), .en(in_1), .clk(Clk_2), .Q(register_2_q));  // open: clr
  Register register_3 (.D(ram_1_dout), .en(in_1), .clk(Clk_2), .Q(register_3_q));  // open: clr
  Register register_4 (.D(register_3_q), .en(in_1), .clk(Clk_2), .Q(out_12));  // open: clr
  Register register_5 (.D(in_9), .en(in_10), .clk(Clk_3), .Q(register_5_q));  // open: clr
  RAM ram_1 (.addr(register_1_q), .we(in_2), .oe(in_4), .clk(Clk), .din(register_5_q), .dout(ram_1_dout));

  // Notes on the sheet:
  //   PC Incrementer
  //   MAR
  //   Write data
  //   PC
  //   MDR
  //   IR
  //   Read data
endmodule
