// Logisim project RegisterFile8X8.circ as structural Verilog: 1 circuit, main circuit main
module main (
  input  [7:0] in_1,
  input  [2:0] ReaAdrs1,
  input  [2:0] WriteAdrs,
  input  [2:0] ReadAdrs2,
  input  Clk,
  output [7:0] ReadPort1,
  output [7:0] ReadPort2
);

  wire decoder_1_out0, decoder_1_out1, decoder_1_out2, decoder_1_out3, decoder_1_out4, decoder_1_out5,
       decoder_1_out6, decoder_1_out7;
  wire [7:0] register_1_q, register_2_q, register_3_q, register_4_q, register_5_q, register_6_q,
       register_7_q, register_8_q;

  Decoder #(.select(3)) decoder_1 (
    .out0(decoder_1_out0), .out1(decoder_1_out1), .out2(decoder_1_out2), .out3(decoder_1_out3),
    .out4(decoder_1_out4), .out5(decoder_1_out5), .out6(decoder_1_out6), .out7(decoder_1_out7),
    .sel(WriteAdrs));  // open: en
  Register register_1 (.D(in_1), .en(decoder_1_out0), .clk(Clk), .Q(register_1_q));  // open: clr
  Register register_2 (.D(in_1), .en(decoder_1_out2), .clk(Clk), .Q(register_2_q));  // open: clr
  Register register_3 (.D(in_1), .en(decoder_1_out4), .clk(Clk), .Q(register_3_q));  // open: clr
  Register register_4 (.D(in_1), .en(decoder_1_out6), .clk(Clk), .Q(register_4_q));  // open: clr
  Register register_5 (.D(in_1), .en(decoder_1_out1), .clk(Clk), .Q(register_5_q));  // open: clr
  Register register_6 (.D(in_1), .en(decoder_1_out3), .clk(Clk), .Q(register_6_q));  // open: clr
  Register register_7 (.D(in_1), .en(decoder_1_out5), .clk(Clk), .Q(register_7_q));  // open: clr
  Register register_8 (.D(in_1), .en(decoder_1_out7), .clk(Clk), .Q(register_8_q));  // open: clr
  Multiplexer #(.select(3), .width(8)) multiplexer_1 (
    .in0(register_1_q), .in1(register_5_q), .in2(register_2_q), .in3(register_6_q), .in4(register_3_q),
    .in5(register_7_q), .in6(register_4_q), .in7(register_8_q), .out(ReadPort1), .sel(ReaAdrs1));
  Multiplexer #(.select(3), .width(8)) multiplexer_2 (
    .in0(register_1_q), .in1(register_5_q), .in2(register_2_q), .in3(register_6_q), .in4(register_3_q),
    .in5(register_7_q), .in6(register_4_q), .in7(register_8_q), .out(ReadPort2), .sel(ReadAdrs2));

  // Notes on the sheet:
  //   WriteData
  //   000
  //   010
  //   100
  //   110
  //   001
  //   011
  //   101
  //   111
endmodule
