// Logisim project processor.circ as structural Verilog: 11 circuits, main circuit main
module main (
  input  in_1,
  input  in_2,
  input  in_3,
  input  [11:0] in_4,
  output [3:0] N_Z_C_V,
  output [7:0] out_6,
  output [7:0] out_7,
  output [7:0] out_8
);

  wire clock_1_out;
  wire [2:0] controlunit_1_destn, controlunit_1_out_2, controlunit_1_out_3, controlunit_1_out_5;
  wire [3:0] alu_1_nzcv;
  wire [7:0] mar_1_out_3, programcounter_1_out_3;
  wire [11:0] ir_1_out_3, mdr_1_out_3, ram_1_dout;

  Clock clock_1 (.out(clock_1_out));
  RAM #(.dataWidth(12)) ram_1 (
    .addr(mar_1_out_3), .we(in_1), .oe(in_3), .clk(clock_1_out), .din(in_4), .dout(ram_1_dout));
  MAR mar_1 (.in_1(programcounter_1_out_3), .in_2(clock_1_out), .out_3(mar_1_out_3));
  MDR mdr_1 (.in_1(ram_1_dout), .in_2(clock_1_out), .out_3(mdr_1_out_3));
  IR ir_1 (.in_1(mdr_1_out_3), .in_2(clock_1_out), .out_3(ir_1_out_3));
  programCounter programcounter_1 (.in_1(in_2), .in_2(clock_1_out), .out_3(programcounter_1_out_3));
  registerFile registerfile_1 (
    .in_1(out_8), .in_2(controlunit_1_destn), .ReaAdrs1(controlunit_1_out_2),
    .ReadAdrs2(controlunit_1_out_3), .in_5(clock_1_out), .ReadPort1(out_6), .ReadPort2(out_7));
  controlUnit controlunit_1 (
    .in_1(ir_1_out_3), .out_2(controlunit_1_out_2), .out_3(controlunit_1_out_3), .destn(controlunit_1_destn),
    .out_5(controlunit_1_out_5));
  ALU alu_1 (.in_1(out_6), .in_2(out_7), .in_3(controlunit_1_out_5), .NZCV(alu_1_nzcv), .out_5(out_8));
  statusRegister statusregister_1 (.in_1(alu_1_nzcv), .in_2(clock_1_out), .out_3(N_Z_C_V));

  // Notes on the sheet:
  //   Opcode Format:
  //   add - 000
  //   oprtn (3) destn (3) src1(3) src2(3)
  //   sub - 001
  //   opcode
  //   instruction memory
  //   Processor 8 bit
  //   operand1
  //   operand2
  //   result
endmodule

module registerFile (
  input  [7:0] in_1,
  input  [2:0] in_2,
  input  [2:0] ReaAdrs1,
  input  [2:0] ReadAdrs2,
  input  in_5,
  output [7:0] ReadPort1,
  output [7:0] ReadPort2
);

  wire decoder_1_out0, decoder_1_out1, decoder_1_out2, decoder_1_out3, decoder_1_out4, decoder_1_out5,
       decoder_1_out6, decoder_1_out7;
  wire [7:0] R0_q, R1_q, R2_q, R3_q, R4_q, R5_q, R6_q, R7_q;

  Decoder #(.select(3)) decoder_1 (
    .out0(decoder_1_out0), .out1(decoder_1_out1), .out2(decoder_1_out2), .out3(decoder_1_out3),
    .out4(decoder_1_out4), .out5(decoder_1_out5), .out6(decoder_1_out6), .out7(decoder_1_out7), .sel(in_2));  // open: en
  Register R0 (.D(in_1), .en(decoder_1_out0), .clk(in_5), .Q(R0_q));  // open: clr
  Register R2 (.D(in_1), .en(decoder_1_out2), .clk(in_5), .Q(R2_q));  // open: clr
  Register R4 (.D(in_1), .en(decoder_1_out4), .clk(in_5), .Q(R4_q));  // open: clr
  Register R6 (.D(in_1), .en(decoder_1_out6), .clk(in_5), .Q(R6_q));  // open: clr
  Register R1 (.D(in_1), .en(decoder_1_out1), .clk(in_5), .Q(R1_q));  // open: clr
  Register R3 (.D(in_1), .en(decoder_1_out3), .clk(in_5), .Q(R3_q));  // open: clr
  Register R5 (.D(in_1), .en(decoder_1_out5), .clk(in_5), .Q(R5_q));  // open: clr
  Register R7 (.D(in_1), .en(decoder_1_out7), .clk(in_5), .Q(R7_q));  // open: clr
  Multiplexer #(.select(3), .width(8)) multiplexer_1 (
    .in0(R0_q), .in1(R1_q), .in2(R2_q), .in3(R3_q), .in4(R4_q), .in5(R5_q), .in6(R6_q), .in7(R7_q),
    .out(ReadPort1), .sel(ReaAdrs1));
  Multiplexer #(.select(3), .width(8)) multiplexer_2 (
    .in0(R0_q), .in1(R1_q), .in2(R2_q), .in3(R3_q), .in4(R4_q), .in5(R5_q), .in6(R6_q), .in7(R7_q),
    .out(ReadPort2), .sel(ReadAdrs2));

  // Notes on the sheet:
  //   WriteAdrs
  //   Clk
  //   WriteData
  //   000
  //   010
  //   100
  //   110
  //   001
  //   011
  //   101
  //   111
endmodule

module ALU (
  input  [7:0] in_1,
  input  [7:0] in_2,
  input  [2:0] in_3,
  output [3:0] NZCV,
  output [7:0] out_5
);

  wire [3:0] adder8bit_1_n_z_c_v, substractor8bit_1_n_z_c_v;
  wire [7:0] adder8bit_1_out_4, substractor8bit_1_out_4;

  adder8Bit adder8bit_1 (.in_1(in_1), .in_2(in_2), .N_Z_C_V(adder8bit_1_n_z_c_v), .out_4(adder8bit_1_out_4));
  substractor8Bit substractor8bit_1 (
    .in_1(in_1), .in_2(in_2), .N_Z_C_V(substractor8bit_1_n_z_c_v), .out_4(substractor8bit_1_out_4));
  Multiplexer #(.select(3), .width(4)) multiplexer_1 (
    .in0(adder8bit_1_n_z_c_v), .in1(substractor8bit_1_n_z_c_v), .out(NZCV), .sel(in_3));  // open: in2, in3, in4, in5, in6, in7
  Multiplexer #(.select(3), .width(8)) multiplexer_2 (
    .in0(adder8bit_1_out_4), .in1(substractor8bit_1_out_4), .out(out_5), .sel(in_3));  // open: in2, in3, in4, in5, in6, in7

  // Notes on the sheet:
  //   flags
  //   result
  //   flags
  //   result
  //   flag mux
  //   result mux
  //   to Status Reg
  //   flags
  //   result
endmodule

module adder8Bit (
  input  [7:0] in_1,
  input  [7:0] in_2,
  output [3:0] N_Z_C_V,
  output [7:0] out_4
);

  wire adder_1_cout, adder_2_cout, adder_3_cout, adder_4_cout, adder_5_cout, adder_6_cout, adder_7_cout;

  Adder #(.width(1)) adder_1 (.a(in_1[0]), .b(in_2[0]), .out(out_4[0]), .cin(1'b0), .cout(adder_1_cout));
  Adder #(.width(1)) adder_2 (.a(in_1[1]), .b(in_2[1]), .out(out_4[1]), .cin(adder_1_cout), .cout(adder_2_cout));
  Adder #(.width(1)) adder_3 (.a(in_1[2]), .b(in_2[2]), .out(out_4[2]), .cin(adder_2_cout), .cout(adder_3_cout));
  Adder #(.width(1)) adder_4 (.a(in_1[3]), .b(in_2[3]), .out(out_4[3]), .cin(adder_3_cout), .cout(adder_4_cout));
  Adder #(.width(1)) adder_5 (.a(in_1[4]), .b(in_2[4]), .out(out_4[4]), .cin(adder_4_cout), .cout(adder_5_cout));
  Adder #(.width(1)) adder_6 (.a(in_1[5]), .b(in_2[5]), .out(out_4[5]), .cin(adder_5_cout), .cout(adder_6_cout));
  Adder #(.width(1)) adder_7 (.a(in_1[6]), .b(in_2[6]), .out(out_4[6]), .cin(adder_6_cout), .cout(adder_7_cout));
  Adder #(.width(1)) adder_8 (.a(in_1[7]), .b(in_2[7]), .out(N_Z_C_V[3]), .cin(adder_7_cout), .cout(N_Z_C_V[1]));
  xor xor_1 (N_Z_C_V[0], adder_7_cout, N_Z_C_V[1]);
  Comparator comparator_1 (.a({N_Z_C_V[3], out_4[6:0]}), .b({8{1'b0}}), .eq(N_Z_C_V[2]));  // open: gt, lt

  assign out_4[7] = N_Z_C_V[3];
endmodule

module substractor8Bit (
  input  [7:0] in_1,
  input  [7:0] in_2,
  output [3:0] N_Z_C_V,
  output [7:0] out_4
);

  wire adder_2_cout, adder_3_cout, adder_4_cout, adder_5_cout, adder_6_cout, adder_7_cout, adder_8_cout;
  wire [7:0] adder_1_out, not_1_out;

  assign not_1_out = ~in_2;  // NOT_Gate not_1, 8 bits wide
  Adder adder_1 (.a(not_1_out), .b(8'h1), .out(adder_1_out));  // open: cin, cout
  Adder #(.width(1)) adder_2 (.a(in_1[0]), .b(adder_1_out[0]), .out(out_4[0]), .cin(1'b0), .cout(adder_2_cout));
  Adder #(.width(1)) adder_3 (.a(in_1[1]), .b(adder_1_out[1]), .out(out_4[1]), .cin(adder_2_cout), .cout(adder_3_cout));
  Adder #(.width(1)) adder_4 (.a(in_1[2]), .b(adder_1_out[2]), .out(out_4[2]), .cin(adder_3_cout), .cout(adder_4_cout));
  Adder #(.width(1)) adder_5 (.a(in_1[3]), .b(adder_1_out[3]), .out(out_4[3]), .cin(adder_4_cout), .cout(adder_5_cout));
  Adder #(.width(1)) adder_6 (.a(in_1[4]), .b(adder_1_out[4]), .out(out_4[4]), .cin(adder_5_cout), .cout(adder_6_cout));
  Adder #(.width(1)) adder_7 (.a(in_1[5]), .b(adder_1_out[5]), .out(out_4[5]), .cin(adder_6_cout), .cout(adder_7_cout));
  Adder #(.width(1)) adder_8 (.a(in_1[6]), .b(adder_1_out[6]), .out(out_4[6]), .cin(adder_7_cout), .cout(adder_8_cout));
  Adder #(.width(1)) adder_9 (.a(in_1[7]), .b(adder_1_out[7]), .out(N_Z_C_V[3]), .cin(adder_8_cout), .cout(N_Z_C_V[1]));
  xor xor_1 (N_Z_C_V[0], adder_8_cout, N_Z_C_V[1]);
  Comparator comparator_1 (.a({N_Z_C_V[3], out_4[6:0]}), .b({8{1'b0}}), .eq(N_Z_C_V[2]));  // open: gt, lt

  assign out_4[7] = N_Z_C_V[3];
endmodule

module programCounter (
  input  in_1,
  input  in_2,
  output [7:0] out_3
);

  wire [7:0] adder_1_out, multiplexer_1_out;

  Adder adder_1 (.a(8'h1), .b(out_3), .out(adder_1_out));  // open: cin, cout
  Register register_1 (.D(multiplexer_1_out), .clk(in_2), .Q(out_3));  // open: en, clr
  Multiplexer #(.width(8)) multiplexer_1 (.in0({8{1'b0}}), .in1(adder_1_out), .out(multiplexer_1_out), .sel(in_1));

  // Notes on the sheet:
  //   pc incrementor
  //   initial adrs
endmodule

module IR (
  input  [11:0] in_1,
  input  in_2,
  output [11:0] out_3
);

  Register #(.width(12)) register_1 (.D(in_1), .clk(in_2), .Q(out_3));  // open: en, clr
endmodule

module MDR (
  input  [11:0] in_1,
  input  in_2,
  output [11:0] out_3
);

  Register #(.width(12)) register_1 (.D(in_1), .clk(in_2), .Q(out_3));  // open: en, clr
endmodule

module controlUnit (
  input  [11:0] in_1,
  output [2:0] out_2,
  output [2:0] out_3,
  output [2:0] destn,
  output [2:0] out_5
);


  assign destn = in_1[8:6];
  assign out_2 = in_1[2:0];
  assign out_3 = in_1[5:3];
  assign out_5 = in_1[11:9];

  // Notes on the sheet:
  //   MSB
  //   oprtn (3) destn (3) src1(3) src2(3)
  //   LSB
  //   operation selector in ALU
  //   src2
  //   src1
endmodule

module MAR (
  input  [7:0] in_1,
  input  in_2,
  output [7:0] out_3
);

  Register register_1 (.D(in_1), .clk(in_2), .Q(out_3));  // open: en, clr
endmodule

module statusRegister (
  input  [3:0] in_1,
  input  in_2,
  output [3:0] out_3
);

  Register #(.width(4)) register_1 (.D(in_1), .clk(in_2), .Q(out_3));  // open: en, clr
endmodule
